// Logisim project parte1_memoria.circ as structural Verilog
module main (
  input  in_1,
  input  A5,
  input  in_3,
  input  A4,
  input  in_5,
  input  A3,
  input  in_7,
  input  A2,
  input  in_9,
  input  A1,
  input  in_11,
  input  A0,
  input  in_13,
  input  in_14
);

  _74139 #(.ShowInternalStructure("true")) Decodificador ();  // open: pin1, pin2, pin3, pin4, pin5, pin6, pin7, pin15, pin14, pin13, pin12, pin11, pin10, pin9
  ROM rom_1 ();  // open: addr, data
  RAM #(.dataWidth(6), .\type ("nonvolatile")) ram_1 ();  // open: addr, we, oe, clk, din, dout
  Register BancoDeRegistradores ();  // open: D, en, clk, Q, clr

  // Notes on the sheet:
  //   6 bits de endereçamento ( A5 . . . A0)
  //   8 bits de endereçamento de dados
endmodule
