// Logisim project parte1_cache.circ as structural Verilog: 4 circuits, main circuit main
module main (
  input  [5:0] Endereco,
  input  [15:0] entradaDados,
  input  Clock,
  input  Resetar,
  output ACERTO,
  output [3:0] Contador,
  output [7:0] DADO_LIDO,
  output FALTA
);

  wire a, and_1_out, and_2_out, and_3_out, and_4_out, and_5_out, and_6_out, b, c, d, decoder_1_out0,
       decoder_1_out1, decoder_1_out2, decoder_1_out3, e, f, g, L0_ANDmiss_out, l0_q, L1_AND_MISS_out, l1_q,
       L2_AND_MISS_out, l2_q, L3_AND_MISS_out, l3_q, multiplexer_1_out, not_1_out, not_2_out, not_3_out,
       not_4_out, not_5_out, not_6_out, not_7_out, or_5_out, or_6_out, or_7_out, or_8_out;
  wire [2:0] TAG_dout;
  wire [3:0] or_1_out;
  wire [15:0] Dados_dout;

  // Probe on Endereco
  D_Flip_Flop l0 (.D(or_1_out[0]), .clk(Clock), .Q(l0_q), .reset(Resetar));  // open: Qn, preset
  D_Flip_Flop l1 (.D(or_1_out[1]), .clk(Clock), .Q(l1_q), .reset(Resetar));  // open: Qn, preset
  D_Flip_Flop l2 (.D(or_1_out[2]), .clk(Clock), .Q(l2_q), .reset(Resetar));  // open: Qn, preset
  D_Flip_Flop l3 (.D(or_1_out[3]), .clk(Clock), .Q(l3_q), .reset(Resetar));  // open: Qn, preset
  or or_1 (or_1_out[0], l0_q, L0_ANDmiss_out);
  or or_2 (or_1_out[1], l1_q, L1_AND_MISS_out);
  or or_3 (or_1_out[2], l2_q, L2_AND_MISS_out);
  or or_4 (or_1_out[3], l3_q, L3_AND_MISS_out);
  // Probe on Endereco[0]
  // Probe on Endereco[2:1]
  // Probe on Endereco[5:3]
  Decoder #(.select(2)) decoder_1 (
    .out0(decoder_1_out0), .out1(decoder_1_out1), .out2(decoder_1_out2), .out3(decoder_1_out3),
    .sel(Endereco[2:1]));  // open: en
  Multiplexer #(.select(2)) multiplexer_1 (
    .in0(l0_q), .in1(l1_q), .in2(l2_q), .in3(l3_q), .out(multiplexer_1_out), .sel(Endereco[2:1]));
  and L0_ANDmiss (L0_ANDmiss_out, decoder_1_out0, FALTA);
  and L1_AND_MISS (L1_AND_MISS_out, decoder_1_out1, FALTA);
  RAM #(.addrWidth(2), .dataWidth(3)) TAG (
    .addr(Endereco[2:1]), .we(FALTA), .oe(1'b1), .clk(Clock), .din(Endereco[5:3]), .dout(TAG_dout));
  RAM #(.addrWidth(2), .dataWidth(16)) Dados (
    .addr(Endereco[2:1]), .we(FALTA), .oe(1'b1), .clk(Clock), .din(entradaDados), .dout(Dados_dout));
  and L2_AND_MISS (L2_AND_MISS_out, decoder_1_out2, FALTA);
  and L3_AND_MISS (L3_AND_MISS_out, decoder_1_out3, FALTA);
  not not_1 (not_1_out, TAG_dout[1]);
  not not_2 (not_2_out, TAG_dout[2]);
  not not_3 (not_3_out, Endereco[3]);
  not not_4 (not_4_out, Endereco[4]);
  not not_5 (not_5_out, Endereco[5]);
  not not_6 (not_6_out, TAG_dout[0]);
  Multiplexer #(.width(8)) multiplexer_2 (
    .in0(Dados_dout[7:0]), .in1(Dados_dout[15:8]), .out(DADO_LIDO), .sel(Endereco[0]));
  and and_1 (and_1_out, not_3_out, TAG_dout[0]);
  or or_5 (or_5_out, and_1_out, and_2_out);
  and and_2 (and_2_out, Endereco[3], not_6_out);
  and and_3 (and_3_out, not_4_out, TAG_dout[0]);
  or or_6 (or_6_out, and_3_out, and_4_out);
  and and_4 (and_4_out, Endereco[4], TAG_dout[1]);
  and and_5 (and_5_out, not_5_out, TAG_dout[2]);
  or or_7 (or_7_out, and_5_out, and_6_out);
  and and_6 (and_6_out, Endereco[5], not_2_out);
  or or_8 (or_8_out, or_5_out, or_6_out, or_7_out);
  not not_7 (not_7_out, or_8_out);
  and and_7 (ACERTO, not_7_out, multiplexer_1_out);
  not not_8 (FALTA, ACERTO);
  Counter #(.max('hf), .width(4)) counter_1 (
    .clr(Resetar), .count(ACERTO), .clk(Clock), .Q(Contador));  // open: load, up, D, carry
  _7_Segment_Display u_7_segment_display_1 (.g(g), .f(f), .a(a), .b(b), .e(e), .d(d), .c(c));  // open: dp
  Decodificador7seg decodificador7seg_1 (.contador(Contador), .a(a), .b(b), .c(c), .d(d), .e(e), .f(f), .g(g));

  // Notes on the sheet:
  //   bits validos 0 - 3
  //   ATIVA BIT VALIDO SEM SOBRESCREVER ESTADO ANTERIOR
  //   0 - deslocamento
  //   2-1 indice 
  //   5-3 tag
  //   TAG da linha acessada S0 - S2
  //   2 bytes
  //   TAG enderecamento
  //   T0 - T2
  //   xor t0s0
  //   xor t1s1
  //   xor t2s2
  //   iguais
  //   iguais . valido[indice]
  //   MISS
  //   HIT
endmodule

module teste_conflito (
  input  clockV,
  input  [15:0] Dados,
  input  clockCache,
  input  Reset,
  output offset,
  output [1:0] indice,
  output [2:0] tag,
  output [2:0] bitV,
  output [5:0] endereco,
  output acerto,
  output Primo,
  output [3:0] contador,
  output [7:0] dadoLido,
  output falta
);

  wire [7:6] adder_1_out;

  Counter #(.max('h7), .width(3)) V (.Q(bitV), .clk(clockV), .clr(Reset));  // open: load, D, count, carry, up
  main main_1 (
    .Endereco(endereco), .entradaDados(Dados), .Clock(clockCache), .Resetar(Reset), .ACERTO(acerto),
    .Contador(contador), .DADO_LIDO(dadoLido), .FALTA(falta));
  detectorPrimo4b detectorprimo4b_1 (.V({1'b0, bitV}), .Primo(Primo));
  Adder adder_1 (.a({2'b00, bitV, 3'b000}), .b({8{1'b0}}), .out({adder_1_out, endereco}), .cin(1'b0));  // open: cout

  assign indice = endereco[2:1];
  assign offset = endereco[0];
  assign tag = endereco[5:3];

  // Other names for the same wires on the sheet: fim[5:0] = endereco

  // Notes on the sheet:
  //   Cache
  //   <- tag advinda do contador
  //   se conecta ao tunel de mesmo nome, que faz ligação com o endereço recebido pela cache
endmodule

module detectorPrimo4b (
  input  [3:0] V,
  output Primo
);

  wire and_1_out, and_2_out, and_3_out, and_4_out, not_1_out, not_2_out, not_3_out;

  not not_1 (not_1_out, V[3]);
  not not_2 (not_2_out, V[2]);
  not not_3 (not_3_out, V[1]);
  and and_1 (and_1_out, not_1_out, not_2_out, V[1]);
  and and_2 (and_2_out, not_2_out, V[1], V[0]);
  and and_3 (and_3_out, V[2], not_3_out, V[0]);
  and and_4 (and_4_out, not_1_out, V[1], V[0]);
  or or_1 (Primo, and_1_out, and_2_out, and_3_out, and_4_out);
endmodule

module Decodificador7seg (
  input  [3:0] contador,
  output a,
  output b,
  output c,
  output d,
  output e,
  output f,
  output g
);

  wire and_1_out, and_2_out, and_3_out, and_4_out, and_5_out, and_6_out, and_7_out, and_8_out, and_9_out,
       and_10_out, and_11_out, and_12_out, and_13_out, and_14_out, and_15_out, and_16_out, and_17_out,
       and_18_out, not_1_out, not_2_out, not_3_out, not_4_out;

  not not_1 (not_1_out, contador[3]);
  not not_2 (not_2_out, contador[2]);
  not not_3 (not_3_out, contador[1]);
  not not_4 (not_4_out, contador[0]);
  and and_1 (and_1_out, not_1_out, not_2_out, not_4_out);
  and and_2 (and_2_out, not_2_out, contador[1], contador[0]);
  and and_3 (and_3_out, contador[2], not_3_out, contador[0]);
  and and_4 (and_4_out, not_1_out, contador[1], contador[0]);
  and and_5 (and_5_out, not_3_out, not_4_out);
  and and_6 (and_6_out, contador[1], contador[0]);
  or or_1 (c, not_3_out, contador[0], contador[2]);
  and and_7 (and_7_out, not_2_out, not_4_out);
  and and_8 (and_8_out, not_2_out, contador[1]);
  and and_9 (and_9_out, contador[2], not_3_out, contador[0]);
  and and_10 (and_10_out, contador[1], not_4_out);
  and and_11 (and_11_out, not_2_out, not_4_out);
  and and_12 (and_12_out, contador[1], not_4_out);
  and and_13 (and_13_out, not_3_out, not_4_out);
  and and_14 (and_14_out, contador[2], not_3_out);
  and and_15 (and_15_out, contador[2], not_4_out);
  and and_16 (and_16_out, not_2_out, contador[1]);
  and and_17 (and_17_out, contador[2], not_3_out);
  and and_18 (and_18_out, contador[1], not_4_out);
  or or_2 (a, and_1_out, and_2_out, and_3_out, and_4_out);
  or or_3 (b, not_2_out, and_5_out, and_6_out);
  or or_4 (d, and_7_out, and_8_out, and_9_out, and_10_out, contador[3]);
  or or_5 (e, and_11_out, and_12_out);
  or or_6 (f, and_13_out, and_14_out, and_15_out, contador[3]);
  or or_7 (g, and_16_out, and_17_out, contador[3], and_18_out);
endmodule
