// Logisim project parte1_memoria.circ as structural Verilog
module main (
  input  A5,
  input  A4,
  input  A3,
  input  A2,
  input  A1,
  input  A0
);

  wire Decodificador_pin1, Decodificador_pin4, Decodificador_pin5, not_1_out, not_2_out;
  wire [7:0] ram_1_dout, rom_1_data;

  _74139 #(.ShowInternalStructure("true")) Decodificador (
    .pin1(Decodificador_pin1), .pin2(A5), .pin3(A4), .pin4(Decodificador_pin4), .pin5(Decodificador_pin5));  // open: pin6, pin7, pin15, pin14, pin13, pin12, pin11, pin10, pin9
  not not_1 (not_1_out, Decodificador_pin4);
  not not_2 (not_2_out, Decodificador_pin5);
  ROM #(.addrWidth(4)) rom_1 (.addr({A3, A2, A1, A0}), .data(rom_1_data));
  RAM #(.addrWidth(4), .\type ("nonvolatile")) ram_1 (
    .addr({A3, A2, A1, A0}), .oe(not_2_out), .dout(ram_1_dout));  // open: we, clk, din
  RAM #(.addrWidth(4)) ram_2 (.addr({A3, A2, A1, A0}));  // open: we, oe, clk, din, dout
  RAM #(.addrWidth(4)) ram_3 (.addr({A3, A2, A1, A0}));  // open: we, oe, clk, din, dout
  assign ram_1_dout = not_1_out ? rom_1_data : 8'bz;  // Controlled_Buffer controlled_buffer_1

  // Notes on the sheet:
  //   6 bits de endereçamento ( A5 . . . A0)
  //   Banco de registradores
  //   E/S
  //   se conecta a cache
endmodule
