// Logisim project parte1_memoria.circ as structural Verilog
module main (
  input  A5,
  input  A4,
  input  A3,
  input  A2,
  input  A1,
  input  A0,
  input  [7:0] DIN,
  input  CLK,
  input  WE,
  output [7:0] out_10
);

  wire and_1_out, and_2_out, and_3_out, and_4_out, Decodificador_pin1, Decodificador_pin4,
       Decodificador_pin5, Decodificador_pin6, Decodificador_pin7, not_1_out, not_2_out, not_3_out,
       not_4_out, odd_parity_1_out, odd_parity_2_out, ram_4_dout, xor_1_out;
  wire [7:0] ram_1_dout, ram_2_dout, ram_3_dout, rom_1_data;

  _74139 #(.ShowInternalStructure("true")) Decodificador (
    .pin1(Decodificador_pin1), .pin2(A4), .pin3(A5), .pin4(Decodificador_pin4), .pin5(Decodificador_pin5),
    .pin6(Decodificador_pin6), .pin7(Decodificador_pin7));  // open: pin15, pin14, pin13, pin12, pin11, pin10, pin9
  not not_1 (not_1_out, Decodificador_pin4);
  not not_2 (not_2_out, Decodificador_pin5);
  not not_3 (not_3_out, Decodificador_pin6);
  LED CS_ROM (.in(not_1_out));
  LED CS_RAM (.in(not_2_out));
  LED CS_REG (.in(not_3_out));
  LED CS_IO (.in(not_4_out));
  not not_4 (not_4_out, Decodificador_pin7);
  xor odd_parity_1 (odd_parity_1_out, DIN[0], DIN[1], DIN[2], DIN[3], DIN[4], DIN[5], DIN[6], DIN[7]);
  and and_1 (and_1_out, WE, not_2_out);
  and and_2 (and_2_out, WE, not_3_out);
  and and_3 (and_3_out, WE, not_4_out);
  and and_4 (and_4_out, WE, not_2_out);
  ROM #(.addrWidth(4)) rom_1 (.addr({A3, A2, A1, A0}), .data(rom_1_data));
  RAM #(.addrWidth(4), .\type ("nonvolatile")) ram_1 (
    .addr({A3, A2, A1, A0}), .we(and_1_out), .oe(not_2_out), .clk(CLK), .din(DIN), .dout(ram_1_dout));
  RAM #(.addrWidth(4), .\type ("nonvolatile")) ram_2 (
    .addr({A3, A2, A1, A0}), .we(and_2_out), .oe(not_3_out), .clk(CLK), .din(DIN), .dout(ram_2_dout));
  RAM #(.addrWidth(4)) ram_3 (
    .addr({A3, A2, A1, A0}), .we(and_3_out), .oe(not_4_out), .clk(CLK), .din(DIN), .dout(ram_3_dout));
  RAM #(.addrWidth(4), .dataWidth(1)) ram_4 (
    .addr({A3, A2, A1, A0}), .we(and_4_out), .oe(not_2_out), .clk(CLK), .din(odd_parity_1_out),
    .dout(ram_4_dout));
  Multiplexer #(.select(2), .width(8)) multiplexer_1 (
    .in0(rom_1_data), .in1(ram_1_dout), .in2(ram_2_dout), .in3(ram_3_dout), .out(out_10), .sel({A5, A4}));
  xor odd_parity_2 (odd_parity_2_out, ram_1_dout[0], ram_1_dout[1], ram_1_dout[2], ram_1_dout[3], ram_1_dout[4], ram_1_dout[5], ram_1_dout[6], ram_1_dout[7]);
  xor xor_1 (xor_1_out, odd_parity_2_out, ram_4_dout);
  LED led_1 (.in(xor_1_out));
  // also tied to GND on the sheet: Decodificador_pin1

  // Notes on the sheet:
  //   6 bits de endereçamento ( A5 . . . A0)
  //   Banco de registradores
  //   E/S
endmodule
