// Logisim project detectorDeSequencia.circ as structural Verilog: 1 circuit, main circuit main
module main (
  input  X,
  output Z
);

  wire and_1_out, clock_1_out, d_ff_1_q, d_ff_2_q, d_ff_2_qn;

  Clock clock_1 (.out(clock_1_out));
  D_Flip_Flop d_ff_1 (.D(and_1_out), .clk(clock_1_out), .Q(d_ff_1_q));  // open: Qn, preset, reset
  D_Flip_Flop d_ff_2 (.D(X), .clk(clock_1_out), .Q(d_ff_2_q), .Qn(d_ff_2_qn));  // open: preset, reset
  and and_1 (and_1_out, d_ff_2_q, ~X);  // AND_Gate
  and and_2 (Z, d_ff_1_q, d_ff_2_qn, X);

  // Notes on the sheet:
  //   Q1
  //   Q0
endmodule
