// Logisim project maquinaDeEstadosUC.circ as structural Verilog: 1 circuit, main circuit main
module main (
  input  OP,
  input  Reset,
  output RegWrite,
  output PcWriteCond,
  output PcSource,
  output PcWrite,
  output MemRead,
  output IRWrite,
  output [1:0] ALUSrcB,
  output ALUSrcA,
  output [1:0] ALUOp
);

  wire and_1_out, and_5_out, and_6_out, and_7_out, and_8_out, clock_1_out, d_ff_1_qn, d_ff_2_qn, d_ff_3_qn,
       not_1_out, or_2_out;

  Clock clock_1 (.out(clock_1_out));
  not not_1 (not_1_out, OP);
  // BCD_to_7_Segment_decoder bcd_to_7_segment_decoder_1: pin names not known; wires that end beside it: {1'b0, ALUOp[0], ALUOp[1], ALUSrcB[1]}
  _7_Segment_Display u_7_segment_display_1 ();  // open: g, f, a, b, e, d, c, dp
  D_Flip_Flop d_ff_1 (.D(and_5_out), .clk(clock_1_out), .Q(ALUOp[0]), .Qn(d_ff_1_qn), .reset(Reset));  // open: preset
  D_Flip_Flop d_ff_2 (.D(or_2_out), .clk(clock_1_out), .Q(ALUOp[1]), .Qn(d_ff_2_qn), .reset(Reset));  // open: preset
  D_Flip_Flop d_ff_3 (.D(and_1_out), .clk(clock_1_out), .Q(ALUSrcB[1]), .Qn(d_ff_3_qn), .reset(Reset));  // open: preset
  and and_1 (and_1_out, d_ff_1_qn, d_ff_3_qn);
  and and_2 (RegWrite, ALUSrcB[1], ~ALUOp[0]);  // AND_Gate
  and and_3 (PcWriteCond, ~ALUSrcB[1], ~ALUOp[1], ALUOp[0]);  // AND_Gate
  and and_4 (ALUSrcB[0], ~ALUSrcB[1], ~ALUOp[1], ~ALUOp[0]);  // AND_Gate
  and and_5 (and_5_out, not_1_out, and_8_out);
  and and_6 (and_6_out, ALUOp[1], d_ff_3_qn);
  and and_7 (and_7_out, OP, and_8_out);
  and and_8 (and_8_out, d_ff_1_qn, d_ff_2_qn, ALUSrcB[1]);
  or or_1 (ALUSrcA, ALUOp[1], ALUOp[0]);
  or or_2 (or_2_out, and_6_out, and_7_out);

  assign IRWrite = ALUSrcB[0];
  assign MemRead = ALUSrcB[0];
  assign PcSource = ALUOp[0];
  assign PcWrite = ALUSrcB[0];

  // Notes on the sheet:
  //   estado atual
  //   Q2
  //   Q1
  //   Q0
  //   LogicaD2
  //   LogicaD0
  //   logicaD1
  //   Sinal de estado S1
  //   a máquina está em S1(001)
endmodule
