// Logisim project parte2_cabeada.circ as structural Verilog: 5 circuits, main circuit main
module main (
  input  ResetGlobal
);

  wire ClockGlobal_out, uccabeada_1_irwrite;

  Clock ClockGlobal (.out(ClockGlobal_out));
  ROM #(.addrWidth(4)) rom_1 ();  // open: addr, data
  UCcabeada uccabeada_1 (
    .Reset(ResetGlobal), .IRWrite(uccabeada_1_irwrite));  // open: OP, RegWrite, PcWriteCond, PcSource, PcWrite, MemRead, ALUSrcB, ALUSrcA, ALUOp
  ULA ula_1 ();  // open: A, B, Op, funct, Zero, Resultado
  IR ir_1 (
    .IRWrite(uccabeada_1_irwrite), .ClockGlobal(ClockGlobal_out), .reset(ResetGlobal));  // open: funct, rd, rt, rs, OP
  bancoReg bancoreg_1 ();  // open: Clock, Reset, EscreverDado, RegWrite, WriteAddr, LerEndereco1, LerEndereco2, R0, R1, LerDado1, LerDado2, R2, R3
endmodule

module bancoReg (
  input  Clock,
  input  Reset,
  input  [7:0] EscreverDado,
  input  RegWrite,
  input  [1:0] WriteAddr,
  input  [1:0] LerEndereco1,
  input  [1:0] LerEndereco2,
  output [7:0] R0,
  output [7:0] R1,
  output [7:0] LerDado1,
  output [7:0] LerDado2,
  output [7:0] R2,
  output [7:0] R3
);

  wire decoder_1_out0, decoder_1_out1, decoder_1_out2, decoder_1_out3;

  Decoder #(.select(2)) decoder_1 (
    .out0(decoder_1_out0), .out1(decoder_1_out1), .out2(decoder_1_out2), .out3(decoder_1_out3),
    .sel(WriteAddr), .en(RegWrite));
  Register reg0 (.D(EscreverDado), .en(decoder_1_out0), .clk(Clock), .Q(R0), .clr(Reset));
  Register reg2 (.D(EscreverDado), .en(decoder_1_out3), .clk(Clock), .Q(R2), .clr(Reset));
  Register reg1 (.D(EscreverDado), .en(decoder_1_out1), .clk(Clock), .Q(R1), .clr(Reset));
  Register reg3 (.D(EscreverDado), .en(decoder_1_out2), .clk(Clock), .Q(R3), .clr(Reset));
  Multiplexer #(.select(2), .width(8)) multiplexer_1 (
    .in0(R0), .in1(R1), .in2(R2), .in3(R3), .out(LerDado1), .sel(LerEndereco1));
  Multiplexer #(.select(2), .width(8)) multiplexer_2 (
    .in0(R0), .in1(R1), .in2(R2), .in3(R3), .out(LerDado2), .sel(LerEndereco2));

  // Other names for the same wires on the sheet: Ler1[1:0] = LerEndereco1; Ler2[1:0] = LerEndereco2
endmodule

module ULA (
  input  [7:0] A,
  input  [7:0] B,
  input  [1:0] Op,
  input  [1:0] funct,
  output Zero,
  output [7:0] Resultado
);

  wire or_2_out;
  wire [7:0] adder_1_out, and_1_out, multiplexer_1_out, or_1_out, subtractor_1_out;

  Adder adder_1 (.a(A), .b(B), .out(adder_1_out), .cin(1'b0));  // open: cout
  Subtractor subtractor_1 (.a(A), .b(B), .out(subtractor_1_out), .bin(1'b0));  // open: bout
  assign and_1_out = A & B;  // AND_Gate and_1, 8 bits wide
  assign or_1_out = A | B;  // OR_Gate or_1, 8 bits wide
  Multiplexer #(.select(2), .width(8)) multiplexer_1 (
    .in0(adder_1_out), .in1(subtractor_1_out), .in2(and_1_out), .in3(or_1_out), .out(multiplexer_1_out),
    .sel(funct));
  Multiplexer #(.select(2), .width(8)) multiplexer_2 (
    .in0(adder_1_out), .in1(subtractor_1_out), .in2(multiplexer_1_out), .in3(or_1_out), .out(Resultado),
    .sel(Op));
  or or_2 (or_2_out, Resultado[0], Resultado[1], Resultado[2], Resultado[3], Resultado[4], Resultado[5], Resultado[6], Resultado[7]);
  not not_1 (Zero, or_2_out);
endmodule

module UCcabeada (
  input  OP,
  input  Reset,
  output RegWrite,
  output PcWriteCond,
  output PcSource,
  output PcWrite,
  output MemRead,
  output IRWrite,
  output [1:0] ALUSrcB,
  output ALUSrcA,
  output [1:0] ALUOp
);

  wire and_1_out, and_5_out, and_6_out, and_7_out, and_8_out, clock_1_out, d_ff_1_qn, d_ff_2_qn, d_ff_3_qn,
       not_1_out, or_2_out;

  Clock clock_1 (.out(clock_1_out));
  not not_1 (not_1_out, OP);
  // BCD_to_7_Segment_decoder bcd_to_7_segment_decoder_1: pin names not known; wires that end beside it: {1'b0, ALUOp[0], ALUOp[1], ALUSrcB[1]}
  _7_Segment_Display u_7_segment_display_1 ();  // open: g, f, a, b, e, d, c, dp
  D_Flip_Flop d_ff_1 (.D(and_5_out), .clk(clock_1_out), .Q(ALUOp[0]), .Qn(d_ff_1_qn), .reset(Reset));  // open: preset
  D_Flip_Flop d_ff_2 (.D(or_2_out), .clk(clock_1_out), .Q(ALUOp[1]), .Qn(d_ff_2_qn), .reset(Reset));  // open: preset
  D_Flip_Flop d_ff_3 (.D(and_1_out), .clk(clock_1_out), .Q(ALUSrcB[1]), .Qn(d_ff_3_qn), .reset(Reset));  // open: preset
  and and_1 (and_1_out, d_ff_1_qn, d_ff_3_qn);
  and and_2 (RegWrite, ALUSrcB[1], ~ALUOp[0]);  // AND_Gate
  and and_3 (PcWriteCond, ~ALUSrcB[1], ~ALUOp[1], ALUOp[0]);  // AND_Gate
  and and_4 (ALUSrcB[0], ~ALUSrcB[1], ~ALUOp[1], ~ALUOp[0]);  // AND_Gate
  and and_5 (and_5_out, not_1_out, and_8_out);
  and and_6 (and_6_out, ALUOp[1], d_ff_3_qn);
  and and_7 (and_7_out, OP, and_8_out);
  and and_8 (and_8_out, d_ff_1_qn, d_ff_2_qn, ALUSrcB[1]);
  or or_1 (ALUSrcA, ALUOp[1], ALUOp[0]);
  or or_2 (or_2_out, and_6_out, and_7_out);

  assign IRWrite = ALUSrcB[0];
  assign MemRead = ALUSrcB[0];
  assign PcSource = ALUOp[0];
  assign PcWrite = ALUSrcB[0];

  // Notes on the sheet:
  //   estado atual
  //   Q2
  //   Q1
  //   Q0
  //   LogicaD2
  //   Sinal de estado S1
  //   LogicaD0
  //   logicaD1
  //   a máquina está em S1(001)
endmodule

module IR (
  input  IRWrite,
  input  ClockGlobal,
  input  reset,
  output funct,
  output [1:0] rd,
  output [1:0] rt,
  output [1:0] rs,
  output OP
);

  Register register_1 (.en(IRWrite), .clk(ClockGlobal), .Q({OP, rs, rt, rd, funct}), .clr(reset));  // open: D
endmodule
