// Logisim project parte2_microprogramada.circ as structural Verilog: 6 circuits, main circuit main
module main (
  input  ResetGlobal
);

  wire and_1_out, ClockGlobal, ir_1_op, or_1_out, ucmicroprogramada_1_alusrca, ucmicroprogramada_1_irwrite,
       ucmicroprogramada_1_memread, ucmicroprogramada_1_pcsource, ucmicroprogramada_1_pcwrite,
       ucmicroprogramada_1_pcwritecond, ucmicroprogramada_1_regwrite, Zero;
  wire [1:0] ir_1_funct, ir_1_rs, ir_1_rt, ucmicroprogramada_1_aluop, ucmicroprogramada_1_alusrcb;
  wire [3:0] ir_1_imm;
  wire [7:0] A_q, B_q, bancoreg_1_dado_rs, bancoreg_1_dado_rt, bancoreg_1_r0, bancoreg_1_r1, bancoreg_1_r2,
       bancoreg_1_r3, bit_extender_1_out, multiplexer_1_out, multiplexer_2_out, multiplexer_3_out,
       multiplexer_4_out, PC_q, RegULAout_q, rom_1_data, shifter_1_out, ula_1_resultado;

  Clock u_ClockGlobal (.out(ClockGlobal));
  Register PC (.D(multiplexer_4_out), .en(or_1_out), .clk(ClockGlobal), .Q(PC_q), .clr(ResetGlobal));
  or or_1 (or_1_out, and_1_out, ucmicroprogramada_1_pcwrite);
  ROM rom_1 (.addr(PC_q), .data(rom_1_data));
  and and_1 (and_1_out, ucmicroprogramada_1_pcwritecond, Zero);
  UCmicroprogramada ucmicroprogramada_1 (
    .OP(ir_1_op), .Reset(ResetGlobal), .ALUOp(ucmicroprogramada_1_aluop),
    .ALUSrcB(ucmicroprogramada_1_alusrcb), .ALUSrcA(ucmicroprogramada_1_alusrca),
    .PcWrite(ucmicroprogramada_1_pcwrite), .MemRead(ucmicroprogramada_1_memread),
    .IRWrite(ucmicroprogramada_1_irwrite), .RegWrite(ucmicroprogramada_1_regwrite),
    .PcWriteCond(ucmicroprogramada_1_pcwritecond), .PcSource(ucmicroprogramada_1_pcsource));
  Multiplexer #(.width(8)) multiplexer_1 (
    .in0({8{1'b0}}), .in1(rom_1_data), .out(multiplexer_1_out), .sel(ucmicroprogramada_1_memread));
  IR ir_1 (
    .entrada_inst(multiplexer_1_out), .IRWrite(ucmicroprogramada_1_irwrite), .ClockGlobal(ClockGlobal),
    .reset(ResetGlobal), .imm(ir_1_imm), .funct(ir_1_funct), .rs(ir_1_rs), .rt(ir_1_rt), .OP(ir_1_op));
  assign bit_extender_1_out = {{4{ir_1_imm[3]}}, ir_1_imm};  // Bit_Extender bit_extender_1
  Shifter shifter_1 (.in(bit_extender_1_out), .\dist (3'b010), .out(shifter_1_out));
  bancoReg bancoreg_1 (
    .Clock(ClockGlobal), .Reset(ResetGlobal), .EscreverDado(RegULAout_q),
    .RegWrite(ucmicroprogramada_1_regwrite), .Rd(ir_1_rt), .Ler_rs(ir_1_rs), .Ler_rt(ir_1_rt),
    .R0(bancoreg_1_r0), .R1(bancoreg_1_r1), .Dado_rs(bancoreg_1_dado_rs), .Dado_rt(bancoreg_1_dado_rt),
    .R2(bancoreg_1_r2), .R3(bancoreg_1_r3));
  // Probe on bancoreg_1_r0
  // Probe on bancoreg_1_r1
  // Probe on bancoreg_1_r2
  // Probe on bancoreg_1_r3
  Register A (.D(bancoreg_1_dado_rs), .en(1'b1), .clk(ClockGlobal), .Q(A_q), .clr(ResetGlobal));
  Register B (.D(bancoreg_1_dado_rt), .en(1'b1), .clk(ClockGlobal), .Q(B_q), .clr(ResetGlobal));
  Multiplexer #(.width(8)) multiplexer_2 (
    .in0(PC_q), .in1(A_q), .out(multiplexer_2_out), .sel(ucmicroprogramada_1_alusrca));
  Multiplexer #(.select(2), .width(8)) multiplexer_3 (
    .in0(B_q), .in1(8'h4), .in2(shifter_1_out), .in3({8{1'b0}}), .out(multiplexer_3_out),
    .sel(ucmicroprogramada_1_alusrcb));
  ULA ula_1 (
    .A(multiplexer_2_out), .B(multiplexer_3_out), .funct(ir_1_funct), .ALUOp(ucmicroprogramada_1_aluop),
    .Zero(Zero), .Resultado(ula_1_resultado));
  Register RegULAout (.D(ula_1_resultado), .en(1'b1), .clk(ClockGlobal), .Q(RegULAout_q), .clr(ResetGlobal));
  Multiplexer #(.width(8)) multiplexer_4 (
    .in0(ula_1_resultado), .in1(RegULAout_q), .out(multiplexer_4_out), .sel(ucmicroprogramada_1_pcsource));

  // Notes on the sheet:
  //   contents of rom_1 (hex, n*v repeats v):
  //   a0 0 0 0 c2 0 0 0 22 0 0 0 e4
  //   MemRead
  //   ALUSrcB
  //   ALUSrcA
  //   PCSource
endmodule

module bancoReg (
  input  Clock,
  input  Reset,
  input  [7:0] EscreverDado,
  input  RegWrite,
  input  [1:0] Rd,
  input  [1:0] Ler_rs,
  input  [1:0] Ler_rt,
  output [7:0] R0,
  output [7:0] R1,
  output [7:0] Dado_rs,
  output [7:0] Dado_rt,
  output [7:0] R2,
  output [7:0] R3
);

  wire decoder_1_out0, decoder_1_out1, decoder_1_out2, decoder_1_out3;

  Decoder #(.select(2)) decoder_1 (
    .out0(decoder_1_out0), .out1(decoder_1_out1), .out2(decoder_1_out2), .out3(decoder_1_out3), .sel(Rd),
    .en(RegWrite));
  Register reg0 (.D(EscreverDado), .en(decoder_1_out0), .clk(Clock), .Q(R0), .clr(Reset));
  Register reg2 (.D(EscreverDado), .en(decoder_1_out2), .clk(Clock), .Q(R2), .clr(Reset));
  Register reg1 (.D(EscreverDado), .en(decoder_1_out1), .clk(Clock), .Q(R1), .clr(Reset));
  Register reg3 (.D(EscreverDado), .en(decoder_1_out3), .clk(Clock), .Q(R3), .clr(Reset));
  Multiplexer #(.select(2), .width(8)) multiplexer_1 (
    .in0(R0), .in1(R1), .in2(R2), .in3(R3), .out(Dado_rs), .sel(Ler_rs));
  Multiplexer #(.select(2), .width(8)) multiplexer_2 (
    .in0(R0), .in1(R1), .in2(R2), .in3(R3), .out(Dado_rt), .sel(Ler_rt));

  // Other names for the same wires on the sheet: Ler1[1:0] = Ler_rs; Ler2[1:0] = Ler_rt
endmodule

module ULA (
  input  [7:0] A,
  input  [7:0] B,
  input  [1:0] funct,
  input  [1:0] ALUOp,
  output Zero,
  output [7:0] Resultado
);

  wire or_2_out;
  wire [7:0] adder_1_out, and_1_out, multiplexer_1_out, or_1_out, subtractor_1_out;

  Adder adder_1 (.a(A), .b(B), .out(adder_1_out), .cin(1'b0));  // open: cout
  Subtractor subtractor_1 (.a(A), .b(B), .out(subtractor_1_out), .bin(1'b0));  // open: bout
  assign and_1_out = A & B;  // AND_Gate and_1, 8 bits wide
  assign or_1_out = A | B;  // OR_Gate or_1, 8 bits wide
  Multiplexer #(.select(2), .width(8)) multiplexer_1 (
    .in0(adder_1_out), .in1(subtractor_1_out), .in2(and_1_out), .in3(or_1_out), .out(multiplexer_1_out),
    .sel(funct));
  Multiplexer #(.select(2), .width(8)) multiplexer_2 (
    .in0(adder_1_out), .in1(subtractor_1_out), .in2(multiplexer_1_out), .in3(or_1_out), .out(Resultado),
    .sel(ALUOp));
  or or_2 (or_2_out, Resultado[0], Resultado[1], Resultado[2], Resultado[3], Resultado[4], Resultado[5], Resultado[6], Resultado[7]);
  not not_1 (Zero, or_2_out);
endmodule

module UCcabeada (
  input  OP,
  input  Reset,
  output RegWrite,
  output PcWriteCond,
  output PcSource,
  output PcWrite,
  output MemRead,
  output IRWrite,
  output [1:0] ALUSrcB,
  output ALUSrcA,
  output [1:0] ALUOp
);

  wire and_1_out, and_5_out, and_6_out, and_7_out, and_8_out, clock_1_out, d_ff_1_qn, d_ff_2_qn, d_ff_3_qn,
       not_1_out, or_2_out;

  Clock clock_1 (.out(clock_1_out));
  not not_1 (not_1_out, OP);
  // BCD_to_7_Segment_decoder bcd_to_7_segment_decoder_1: pin names not known; wires that end beside it: {1'b0, ALUOp[0], ALUOp[1], ALUSrcB[1]}
  _7_Segment_Display u_7_segment_display_1 ();  // open: g, f, a, b, e, d, c, dp
  D_Flip_Flop d_ff_1 (.D(and_5_out), .clk(clock_1_out), .Q(ALUOp[0]), .Qn(d_ff_1_qn), .reset(Reset));  // open: preset
  D_Flip_Flop d_ff_2 (.D(or_2_out), .clk(clock_1_out), .Q(ALUOp[1]), .Qn(d_ff_2_qn), .reset(Reset));  // open: preset
  D_Flip_Flop d_ff_3 (.D(and_1_out), .clk(clock_1_out), .Q(ALUSrcB[1]), .Qn(d_ff_3_qn), .reset(Reset));  // open: preset
  and and_1 (and_1_out, d_ff_1_qn, d_ff_3_qn);
  and and_2 (RegWrite, ALUSrcB[1], ALUOp[1], ~ALUOp[0]);  // AND_Gate
  and and_3 (PcWriteCond, ~ALUSrcB[1], ~ALUOp[1], ALUOp[0]);  // AND_Gate
  and and_4 (ALUSrcB[0], ~ALUSrcB[1], ~ALUOp[1], ~ALUOp[0]);  // AND_Gate
  and and_5 (and_5_out, not_1_out, and_8_out);
  and and_6 (and_6_out, ALUOp[1], d_ff_3_qn);
  and and_7 (and_7_out, OP, and_8_out);
  and and_8 (and_8_out, d_ff_1_qn, d_ff_2_qn, ALUSrcB[1]);
  or or_1 (ALUSrcA, ALUOp[1], ALUOp[0]);
  or or_2 (or_2_out, and_6_out, and_7_out);

  assign IRWrite = ALUSrcB[0];
  assign MemRead = ALUSrcB[0];
  assign PcSource = ALUOp[0];
  assign PcWrite = ALUSrcB[0];

  // Notes on the sheet:
  //   estado atual
  //   Q2
  //   Q1
  //   Q0
  //   LogicaD2
  //   Sinal de estado S1
  //   LogicaD0
  //   logicaD1
  //   a máquina está em S1(001)
endmodule

module IR (
  input  [7:0] entrada_inst,
  input  IRWrite,
  input  ClockGlobal,
  input  reset,
  output [3:0] imm,
  output [1:0] funct,
  output [1:0] rs,
  output [1:0] rt,
  output OP
);

  Register register_1 (.D(entrada_inst), .en(IRWrite), .clk(ClockGlobal), .Q({OP, rt, rs, funct, imm[0]}), .clr(reset));

  assign imm[3:1] = {1'b0, funct};

  // Notes on the sheet:
  //   imm2-1
endmodule

module UCmicroprogramada (
  input  OP,
  input  Reset,
  output ALUSrcA,
  output PcWrite,
  output MemRead,
  output RegWrite,
  output PcWriteCond,
  output [1:0] ALUSrcB,
  output IRWrite,
  output PcSource,
  output [1:0] ALUOp
);

  wire clock_1_out, or_1_out;
  wire [1:0] rom_1_data, rom_1_data_2;
  wire [2:0] bcd_to_7_segment_decoder_1_p1;
  wire [2:1] d1_out;

  and and_1 (ALUSrcB[0], ~ALUSrcB[1], ~ALUSrcA);  // AND_Gate
  // Probe on ALUOp
  // Probe on {ALUSrcB[1], ALUSrcA}
  and and_2 (IRWrite, ~rom_1_data_2[1], rom_1_data_2[0]);  // AND_Gate
  // Probe on rom_1_data_2
  and and_3 (RegWrite, rom_1_data_2[1], ~rom_1_data_2[0]);  // AND_Gate
  and and_4 (PcSource, rom_1_data_2[1], rom_1_data_2[0]);
  // Probe on {ALUOp, ALUSrcB[1], ALUSrcA, rom_1_data_2, rom_1_data}
  or or_1 (or_1_out, rom_1_data[0], rom_1_data[1]);
  and d1 (d1_out[1], ~rom_1_data[0], rom_1_data[1], OP);  // AND_Gate
  and d2 (d1_out[2], ~rom_1_data[0], rom_1_data[1], ~OP);  // AND_Gate
  Clock clock_1 (.out(clock_1_out));
  // BCD_to_7_Segment_decoder bcd_to_7_segment_decoder_1: pin names not known; wires that end beside it: {1'b0, bcd_to_7_segment_decoder_1_p1}
  _7_Segment_Display u_7_segment_display_1 ();  // open: g, f, a, b, e, d, c, dp
  Counter #(.max('h7), .width(3)) componente13 (
    .load(or_1_out), .D({d1_out, 1'b0}), .Q(bcd_to_7_segment_decoder_1_p1), .clk(clock_1_out), .clr(Reset));  // open: count, carry, up
  ROM #(.addrWidth(3)) rom_1 (
    .addr(bcd_to_7_segment_decoder_1_p1), .data({ALUOp, ALUSrcB[1], ALUSrcA, rom_1_data_2, rom_1_data}));

  assign MemRead = IRWrite;
  assign PcWrite = ALUSrcB[0];
  assign PcWriteCond = PcSource;

  // Notes on the sheet:
  //   ULAOp
  //   fonte
  //   ação
  //   seq
  //   d0
  //   estado atual
  //   contents of rom_1 (hex, n*v repeats v):
  //   4 22 90 19 5d
endmodule
